# Fritzing sketch TPC Cloud Light 2025 (saved by Fritzing 0.9.9b)
circuit board: 8.46667cm x 5.64444cm

parts:
  S3 = Toggle Switch [package=THT]
  J1 = Power Jack [package=power_jack_slot]
  MCU1 = Raspberry Pi Zero
  Part1 = Logic Level Converter
  S2 = Round Pushbutton
  Part2 = ws2812b [package="smd 2812b"]

nets:
  GND: S3.L1, J1.GNDBREAK, J1.GND, MCU1.pin_6, MCU1.pin_9, MCU1.pin_20, MCU1.pin_39, Part1.GND, S2.leg1, Part2.VSS
  N1: S3.COM, MCU1.pin_7
  N2: J1.PWR, MCU1.pin_2, MCU1.pin_4, Part1.HV, Part2.VDD
  N3: MCU1.pin_1, MCU1.pin_17, Part1.LV
  N4: MCU1.pin_12, Part1.TX_LV
  N5: MCU1.pin_15, S2.leg0
  N6: Part1.TX_HV, Part2.DIN
